// Logisim project ejs_guia1.circ as structural Verilog
module main (
  input  in_1,
  input  in_2,
  input  in_3,
  input  in_4,
  input  in_5,
  input  in_6,
  input  in_7,
  input  in_8,
  input  in_9,
  input  in_10,
  input  in_11,
  input  in_12,
  input  in_13,
  input  in_14,
  input  in_15,
  input  in_signal_9,
  input  in_17,
  input  in_18,
  input  in_19,
  input  in_20,
  input  in_21,
  input  in_22,
  input  in_23,
  input  in_24,
  input  in_25,
  input  in_26,
  input  in_27,
  input  in_28,
  input  in_29,
  input  in_30,
  input  in_31,
  input  in_32,
  input  in_33,
  input  in_34,
  input  in_35,
  input  in_36,
  input  in_37,
  input  in_38,
  input  in_39,
  input  in_40,
  input  in_41,
  input  in_42,
  input  in_43,
  input  in_44,
  input  in_45,
  input  in_46,
  input  in_47,
  input  in_48,
  input  in_49,
  input  in_50,
  input  in_51,
  input  in_52,
  input  in_53,
  input  in_54,
  input  in_55,
  input  in_56,
  input  in_57,
  input  in_58,
  output out_59,
  output out_60,
  output out_61,
  output out_62,
  output out_63,
  output out_64,
  output out_65,
  output out_66,
  output out_67,
  output out_68,
  output out_69,
  output out_70,
  output out_71,
  output out_72,
  output out_73,
  output out_74,
  output out_75,
  output out_76,
  output out_77,
  output out_78,
  output out_79,
  output out_80,
  output out_81,
  output out_82,
  output out_83,
  output out_84,
  output out_85,
  output out_86,
  output out_87,
  output out_88,
  output out_89,
  output out_90,
  output out_91,
  output out_92,
  output out_93,
  output out_94,
  output out_95,
  output out_96,
  output out_97,
  output out_98,
  output out_99,
  output out_100,
  output Carry,
  output out_102,
  output out_103,
  output out_104,
  output out_105
);

  wire and_1_out, and_2_out, and_3_out, and_4_out, and_5_out, and_10_out, and_11_out, and_12_out, and_13_out,
       and_14_out, and_15_out, and_16_out, and_21_out, and_22_out, and_23_out, and_24_out, and_25_out,
       and_26_out, and_27_out, and_28_out, and_29_out, and_30_out, and_31_out, and_32_out, and_33_out,
       and_34_out, and_35_out, and_36_out, and_37_out, and_38_out, and_43_out, and_44_out, and_45_out,
       and_47_out, and_48_out, and_49_out, and_50_out, and_52_out, and_53_out, and_54_out, and_55_out,
       and_56_out, and_57_out, and_58_out, nand_1_out, nor_1_out, nor_3_out, not_1_out, not_2_out, not_3_out,
       not_4_out, not_5_out, not_6_out, not_7_out, not_8_out, not_9_out, not_10_out, not_11_out, not_12_out,
       not_13_out, not_14_out, not_15_out, not_16_out, not_17_out, not_18_out, not_23_out, not_24_out,
       not_25_out, not_26_out, not_27_out, or_6_out, or_8_out, or_9_out, or_10_out, xnor_1_out, xor_1_out,
       xor_2_out, xor_3_out, xor_5_out, xor_7_out, xor_13_out, xor_15_out, xor_17_out, xor_19_out, xor_24_out;

  not not_1 (not_1_out, in_30);
  not not_2 (not_2_out, in_17);
  not not_3 (not_3_out, in_18);
  not not_4 (not_4_out, in_20);
  not not_5 (not_5_out, in_31);
  not not_6 (not_6_out, in_46);
  nand nand_1 (nand_1_out, in_5, in_8);
  nand nand_2 (out_72, in_15, in_15);
  nor nor_1 (nor_1_out, not_2_out, not_3_out);
  not not_7 (not_7_out, nor_1_out);
  ExactlyOne xor_1 (.out(xor_1_out), .in0(in_44), .in1(in_45), .in2(in_46), .in3(in_47));
  and and_1 (and_1_out, in_45, not_6_out);
  nor nor_2 (out_77, not_7_out, not_4_out);
  and and_2 (and_2_out, not_1_out, not_5_out);
  and and_3 (and_3_out, not_1_out, in_31);
  and and_4 (and_4_out, not_5_out, in_30);
  and and_5 (and_5_out, in_30, in_31);
  LED led_1 (.in(xor_1_out));
  or or_1 (out_92, and_1_out, in_47);
  or or_2 (out_94, in_46, in_47);
  nand nand_3 (out_65, nand_1_out, nand_1_out);
  and and_6 (out_82, in_25, and_2_out);
  and and_7 (out_83, in_25, and_3_out);
  and and_8 (out_85, in_25, and_4_out);
  and and_9 (out_87, in_25, and_5_out);
  and and_10 (and_10_out, in_49, in_48);
  or or_3 (out_99, and_10_out, and_11_out);
  xor xor_2 (xor_2_out, in_48, in_49);
  and and_11 (and_11_out, xor_2_out, in_50);
  or or_4 (Carry, and_15_out, and_16_out);
  and and_12 (and_12_out, xnor_1_out, xor_5_out);
  LED led_2 (.in(and_12_out));
  LED led_3 (.in(and_12_out));
  LED led_4 (.in(and_12_out));
  not not_8 (not_8_out, in_6);
  not not_9 (not_9_out, in_11);
  xor xor_3 (xor_3_out, in_42, in_43);
  and and_13 (and_13_out, in_43, in_42);
  and and_14 (and_14_out, in_41, xor_3_out);
  or or_5 (out_93, and_13_out, and_14_out);
  xor xor_4 (out_100, xor_2_out, in_50);
  xnor xnor_1 (xnor_1_out, in_51, in_55);
  and and_15 (and_15_out, in_55, in_51);
  and and_16 (and_16_out, xor_7_out, or_6_out);
  xor xor_5 (xor_5_out, in_51, out_102);
  LED led_5 (.in(and_12_out));
  LED led_6 (.in(and_12_out));
  LED led_7 (.in(and_12_out));
  not not_10 (not_10_out, in_19);
  not not_11 (not_11_out, in_19);
  not not_12 (not_12_out, in_19);
  not not_13 (not_13_out, in_19);
  xor xor_6 (out_90, in_41, xor_3_out);
  xor xor_7 (xor_7_out, in_51, in_55);
  xor xor_8 (out_102, xor_7_out, or_6_out);
  and and_17 (out_61, not_8_out, not_9_out);
  and and_18 (out_66, in_6, not_9_out);
  and and_19 (out_68, not_8_out, in_11);
  and and_20 (out_70, in_6, in_11);
  and and_21 (and_21_out, in_19, in_22);
  and and_22 (and_22_out, not_10_out, in_24);
  and and_23 (and_23_out, in_19, in_24);
  and and_24 (and_24_out, not_11_out, in_27);
  and and_25 (and_25_out, in_19, in_27);
  and and_26 (and_26_out, not_12_out, in_29);
  and and_27 (and_27_out, in_19, in_29);
  and and_28 (and_28_out, not_13_out, in_32);
  and and_29 (and_29_out, in_56, in_52);
  or or_6 (or_6_out, and_29_out, and_30_out);
  LED led_8 (.in(out_102));
  xor xor_9 (out_79, and_21_out, and_22_out);
  xor xor_10 (out_81, and_23_out, and_24_out);
  xor xor_11 (out_86, and_25_out, and_26_out);
  xor xor_12 (out_89, and_27_out, and_28_out);
  xor xor_13 (xor_13_out, in_52, in_56);
  and and_30 (and_30_out, xor_13_out, or_8_out);
  LED led_9 (.in(out_102));
  LED led_10 (.in(out_102));
  and and_31 (and_31_out, in_37, in_33);
  or or_7 (out_91, and_31_out, and_32_out);
  or or_8 (or_8_out, and_33_out, and_34_out);
  xor xor_14 (out_103, xor_13_out, or_8_out);
  not not_14 (not_14_out, in_4);
  not not_15 (not_15_out, in_10);
  and and_32 (and_32_out, xor_15_out, or_9_out);
  and and_33 (and_33_out, in_57, in_53);
  and and_34 (and_34_out, xor_17_out, and_45_out);
  and and_35 (and_35_out, not_14_out, not_15_out);
  and and_36 (and_36_out, in_4, not_15_out);
  and and_37 (and_37_out, not_14_out, in_10);
  and and_38 (and_38_out, in_4, in_10);
  xor xor_15 (xor_15_out, in_33, in_37);
  or or_9 (or_9_out, and_43_out, and_44_out);
  xor xor_16 (out_95, xor_15_out, or_9_out);
  xor xor_17 (xor_17_out, in_53, in_57);
  xor xor_18 (out_104, xor_17_out, and_45_out);
  nor nor_3 (nor_3_out, out_105, out_104, out_103, out_102);
  and and_39 (out_63, and_35_out, in_signal_9);
  and and_40 (out_67, and_36_out, in_signal_9);
  and and_41 (out_69, and_37_out, in_signal_9);
  and and_42 (out_71, and_38_out, in_signal_9);
  and and_43 (and_43_out, in_38, in_34);
  and and_44 (and_44_out, xor_19_out, or_10_out);
  and and_45 (and_45_out, in_58, in_54);
  _7_Segment_Display u_7_segment_display_1 (
    .f(nor_3_out), .a(nor_3_out), .b(nor_3_out), .e(nor_3_out), .d(nor_3_out), .c(nor_3_out));  // open: g, dp
  not not_16 (not_16_out, in_21);
  not not_17 (not_17_out, in_21);
  not not_18 (not_18_out, in_21);
  xor xor_19 (xor_19_out, in_34, in_38);
  or or_10 (or_10_out, and_52_out, and_53_out);
  xor xor_20 (out_96, xor_19_out, or_10_out);
  xor xor_21 (out_105, in_54, in_58);
  and and_46 (out_78, not_16_out, in_23);
  and and_47 (and_47_out, in_21, in_23);
  and and_48 (and_48_out, not_17_out, in_26);
  and and_49 (and_49_out, in_21, in_26);
  and and_50 (and_50_out, not_18_out, in_28);
  and and_51 (out_88, in_21, in_28);
  and and_52 (and_52_out, in_39, in_35);
  and and_53 (and_53_out, xor_24_out, and_54_out);
  xor xor_22 (out_80, and_47_out, and_48_out);
  xor xor_23 (out_84, and_49_out, and_50_out);
  xor xor_24 (xor_24_out, in_35, in_39);
  xor xor_25 (out_97, xor_24_out, and_54_out);
  and and_54 (and_54_out, in_40, in_36);
  xor xor_26 (out_98, in_36, in_40);
  not not_19 (out_59, in_1);
  not not_20 (out_60, in_2);
  not not_21 (out_62, in_3);
  not not_22 (out_64, in_7);
  not not_23 (not_23_out, in_9);
  not not_24 (not_24_out, in_12);
  not not_25 (not_25_out, in_13);
  not not_26 (not_26_out, in_14);
  xor xor_27 (out_73, not_26_out, and_55_out);
  not not_27 (not_27_out, not_26_out);
  and and_55 (and_55_out, not_25_out, and_56_out);
  and and_56 (and_56_out, not_24_out, and_57_out);
  xor xor_28 (out_74, not_25_out, and_56_out);
  and and_57 (and_57_out, not_23_out, 1'b1);
  xor xor_29 (out_75, not_24_out, and_57_out);
  xor xor_30 (out_76, not_23_out, 1'b1);
  and and_58 (and_58_out, not_23_out, not_24_out, not_25_out, not_27_out);
  LED led_11 (.in(and_58_out));

  // Notes on the sheet:
  //   Ej 7 - Demultiplexer de 2
  //   Ej 8 - Codificador 4in-2out + flag
  //   Ej 4 - AND w/2 NAND
  //   Ej 4 - NOT with NANDs
  //   Ej 5 - f(A,B,C) = A.B.C w/2 NOR and NOTs
  //   Ej 11 - 1 bit Full Adder
  //   Ej 11 - 1 bit Full Adder
  //   Ej 9 - Decoder 4 -> 2
  //   Overflow
  //   Ej 10 - Carry Left Shifter 3-4
  //   Negativo
  //   Ej 12B - 4 bit full adder w/flags
  //   Ej 9 - Demultiplexor
  //   Zero
  //   Ej 10 - Carry Left Shifter 3-4
  //   Ej 12A - 4 bit Full adder
  //   but simpler
  //   Ej 13A - 4 Bit inverter
endmodule
