// Logisim project ejs_guia1.circ as structural Verilog
module main (
  input  in_1,
  input  in_2,
  input  in_3,
  input  in_4,
  input  in_5,
  input  in_6,
  input  in_7,
  input  in_signal_9,
  input  in_9,
  input  in_10,
  input  in_11,
  input  in_12,
  input  in_13,
  input  in_14,
  input  in_15,
  input  in_16,
  input  in_17,
  input  in_18,
  input  in_19,
  input  in_20,
  input  in_21,
  input  in_22,
  input  in_23,
  input  in_24,
  input  in_25,
  input  in_26,
  input  in_27,
  input  in_28,
  input  in_29,
  input  in_30,
  input  in_31,
  input  in_32,
  input  in_33,
  input  in_34,
  input  in_35,
  input  in_36,
  input  in_37,
  input  in_38,
  input  in_39,
  input  in_40,
  input  in_41,
  input  in_42,
  input  in_43,
  input  in_44,
  input  in_45,
  input  in_46,
  input  in_47,
  input  in_48,
  input  in_49,
  input  in_50,
  output out_51,
  output out_52,
  output out_53,
  output out_54,
  output out_55,
  output out_56,
  output out_57,
  output out_58,
  output out_59,
  output out_60,
  output out_61,
  output out_62,
  output out_63,
  output out_64,
  output out_65,
  output out_66,
  output out_67,
  output out_68,
  output out_69,
  output out_70,
  output out_71,
  output out_72,
  output out_73,
  output out_74,
  output out_75,
  output out_76,
  output out_77,
  output out_78,
  output out_79,
  output out_80,
  output out_81,
  output out_82,
  output out_83,
  output out_84,
  output out_85,
  output out_86,
  output out_87,
  output out_88,
  output out_89
);

  wire and_1_out, and_2_out, and_3_out, and_4_out, and_5_out, and_10_out, and_11_out, and_12_out, and_13_out,
       and_18_out, and_19_out, and_20_out, and_21_out, and_22_out, and_23_out, and_24_out, and_25_out,
       and_26_out, and_27_out, and_28_out, and_29_out, and_30_out, and_31_out, and_32_out, and_33_out,
       and_34_out, and_35_out, and_40_out, and_41_out, and_42_out, and_43_out, and_45_out, and_46_out,
       and_47_out, and_48_out, and_50_out, and_51_out, and_52_out, and_53_out, nand_1_out, nor_1_out,
       not_1_out, not_2_out, not_3_out, not_4_out, not_5_out, not_6_out, not_7_out, not_8_out, not_9_out,
       not_10_out, not_11_out, not_12_out, not_13_out, not_14_out, not_15_out, not_16_out, not_17_out,
       not_18_out, or_7_out, or_8_out, or_9_out, or_10_out, xor_1_out, xor_2_out, xor_3_out, xor_10_out,
       xor_12_out, xor_14_out, xor_16_out, xor_18_out, xor_22_out;

  not not_1 (not_1_out, in_22);
  not not_2 (not_2_out, in_9);
  not not_3 (not_3_out, in_10);
  not not_4 (not_4_out, in_12);
  not not_5 (not_5_out, in_23);
  not not_6 (not_6_out, in_38);
  nand nand_1 (nand_1_out, in_2, in_4);
  nand nand_2 (out_60, in_7, in_7);
  nor nor_1 (nor_1_out, not_2_out, not_3_out);
  not not_7 (not_7_out, nor_1_out);
  ExactlyOne xor_1 (.out(xor_1_out), .in0(in_36), .in1(in_37), .in2(in_38), .in3(in_39));
  and and_1 (and_1_out, in_37, not_6_out);
  nor nor_2 (out_61, not_7_out, not_4_out);
  and and_2 (and_2_out, not_1_out, not_5_out);
  and and_3 (and_3_out, not_1_out, in_23);
  and and_4 (and_4_out, not_5_out, in_22);
  and and_5 (and_5_out, in_22, in_23);
  LED led_1 (.in(xor_1_out));
  or or_1 (out_76, and_1_out, in_39);
  or or_2 (out_78, in_38, in_39);
  nand nand_3 (out_53, nand_1_out, nand_1_out);
  and and_6 (out_66, in_17, and_2_out);
  and and_7 (out_67, in_17, and_3_out);
  and and_8 (out_69, in_17, and_4_out);
  and and_9 (out_71, in_17, and_5_out);
  and and_10 (and_10_out, in_41, in_40);
  or or_3 (out_83, and_10_out, and_11_out);
  xor xor_2 (xor_2_out, in_40, in_41);
  and and_11 (and_11_out, xor_2_out, in_50);
  not not_8 (not_8_out, in_3);
  not not_9 (not_9_out, in_6);
  xor xor_3 (xor_3_out, in_34, in_35);
  and and_12 (and_12_out, in_35, in_34);
  and and_13 (and_13_out, in_33, xor_3_out);
  or or_4 (out_77, and_12_out, and_13_out);
  xor xor_4 (out_84, xor_2_out, in_50);
  not not_10 (not_10_out, in_11);
  not not_11 (not_11_out, in_11);
  not not_12 (not_12_out, in_11);
  not not_13 (not_13_out, in_11);
  xor xor_5 (out_74, in_33, xor_3_out);
  and and_14 (out_51, not_8_out, not_9_out);
  and and_15 (out_54, in_3, not_9_out);
  and and_16 (out_56, not_8_out, in_6);
  and and_17 (out_58, in_3, in_6);
  and and_18 (and_18_out, in_11, in_14);
  and and_19 (and_19_out, not_10_out, in_16);
  and and_20 (and_20_out, in_11, in_16);
  and and_21 (and_21_out, not_11_out, in_19);
  and and_22 (and_22_out, in_11, in_19);
  and and_23 (and_23_out, not_12_out, in_21);
  and and_24 (and_24_out, in_11, in_21);
  and and_25 (and_25_out, not_13_out, in_24);
  or or_5 (out_85, and_26_out, and_27_out);
  xor xor_6 (out_63, and_18_out, and_19_out);
  xor xor_7 (out_65, and_20_out, and_21_out);
  xor xor_8 (out_70, and_22_out, and_23_out);
  xor xor_9 (out_73, and_24_out, and_25_out);
  and and_26 (and_26_out, in_46, in_42);
  and and_27 (and_27_out, xor_10_out, or_7_out);
  and and_28 (and_28_out, in_29, in_25);
  or or_6 (out_75, and_28_out, and_29_out);
  xor xor_10 (xor_10_out, in_42, in_46);
  or or_7 (or_7_out, and_30_out, and_31_out);
  xor xor_11 (out_86, xor_10_out, or_7_out);
  not not_14 (not_14_out, in_1);
  not not_15 (not_15_out, in_5);
  and and_29 (and_29_out, xor_12_out, or_8_out);
  and and_30 (and_30_out, in_47, in_43);
  and and_31 (and_31_out, xor_14_out, or_9_out);
  and and_32 (and_32_out, not_14_out, not_15_out);
  and and_33 (and_33_out, in_1, not_15_out);
  and and_34 (and_34_out, not_14_out, in_5);
  and and_35 (and_35_out, in_1, in_5);
  xor xor_12 (xor_12_out, in_25, in_29);
  or or_8 (or_8_out, and_40_out, and_41_out);
  xor xor_13 (out_79, xor_12_out, or_8_out);
  xor xor_14 (xor_14_out, in_43, in_47);
  xor xor_15 (out_87, xor_14_out, or_9_out);
  and and_36 (out_52, and_32_out, in_signal_9);
  and and_37 (out_55, and_33_out, in_signal_9);
  and and_38 (out_57, and_34_out, in_signal_9);
  and and_39 (out_59, and_35_out, in_signal_9);
  and and_40 (and_40_out, in_30, in_26);
  and and_41 (and_41_out, xor_16_out, or_10_out);
  and and_42 (and_42_out, in_48, in_44);
  or or_9 (or_9_out, and_42_out, and_43_out);
  not not_16 (not_16_out, in_13);
  not not_17 (not_17_out, in_13);
  not not_18 (not_18_out, in_13);
  xor xor_16 (xor_16_out, in_26, in_30);
  or or_10 (or_10_out, and_50_out, and_51_out);
  xor xor_17 (out_80, xor_16_out, or_10_out);
  xor xor_18 (xor_18_out, in_44, in_48);
  and and_43 (and_43_out, xor_18_out, and_52_out);
  and and_44 (out_62, not_16_out, in_15);
  and and_45 (and_45_out, in_13, in_15);
  and and_46 (and_46_out, not_17_out, in_18);
  and and_47 (and_47_out, in_13, in_18);
  and and_48 (and_48_out, not_18_out, in_20);
  and and_49 (out_72, in_13, in_20);
  and and_50 (and_50_out, in_31, in_27);
  and and_51 (and_51_out, xor_22_out, and_53_out);
  xor xor_19 (out_88, xor_18_out, and_52_out);
  xor xor_20 (out_64, and_45_out, and_46_out);
  xor xor_21 (out_68, and_47_out, and_48_out);
  xor xor_22 (xor_22_out, in_27, in_31);
  xor xor_23 (out_81, xor_22_out, and_53_out);
  and and_52 (and_52_out, in_49, in_45);
  and and_53 (and_53_out, in_32, in_28);
  xor xor_24 (out_89, in_45, in_49);
  xor xor_25 (out_82, in_28, in_32);

  // Notes on the sheet:
  //   Ej 7 - Demultiplexer de 2
  //   Ej 8 - Codificador 4in-2out + flag
  //   Ej 4 - AND w/2 NAND
  //   Ej 4 - NOT with NANDs
  //   Ej 5 - f(A,B,C) = A.B.C w/2 NOR and NOTs
  //   Ej 11 - 1 bit Full Adder
  //   Ej 11 - 1 bit Full Adder
  //   Ej 9 - Decoder 4 -> 2
  //   Ej 10 - Carry Left Shifter 3-4
  //   Ej 9 - Demultiplexor
  //   Ej 10 - Carry Left Shifter 3-4
  //   Ej 12A - 4 bit Full adder
  //   but simpler
endmodule
