// Logisim project ejs_guia1_seq.circ as structural Verilog: 9 circuits, main circuit main
module main (
);

  fourBitRestricted fourbitrestricted_1 ();  // open: data, clk, load, read, Q, nQ
endmodule

module FFD (
  input  D,
  input  clk,
  input  enable,
  output Q,
  output nQ
);

  wire and_1_out, and_2_out, and_3_out, and_4_out, and_5_out, not_1_out, not_2_out, not_3_out;

  and and_1 (and_1_out, clk, enable);
  not not_1 (not_1_out, D);
  and and_2 (and_2_out, D, and_1_out);
  not not_2 (not_2_out, and_2_out);
  and and_3 (and_3_out, and_1_out, not_1_out);
  not not_3 (not_3_out, and_3_out);
  and and_4 (and_4_out, nQ, not_2_out);
  and and_5 (and_5_out, not_3_out, Q);
  not not_4 (Q, and_4_out);
  not not_5 (nQ, and_5_out);
endmodule

module newALU (
  input  enable,
  input  [3:0] loadA,
  input  [3:0] loadB,
  input  sum,
  input  res,
  input  bwand,
  input  bwor,
  input  read,
  output [3:0] Q,
  output out_10,
  output out_11,
  output out_12,
  output out_13
);

  wire clock_1_out, priority_encoder_1_gs;
  wire [1:0] priority_encoder_1_out;
  wire [3:0] alu_1_s, fourbitreg_1_q, fourbitreg_2_q;

  Clock clock_1 (.out(clock_1_out));
  Priority_Encoder #(.select(2)) priority_encoder_1 (
    .in0(sum), .in1(res), .in2(bwand), .in3(bwor), .out(priority_encoder_1_out), .gs(priority_encoder_1_gs));  // open: en_out, en_in
  fourBitReg fourbitreg_1 (.D(loadA), .clk(clock_1_out), .enable(enable), .Q(fourbitreg_1_q));
  fourBitReg fourbitreg_2 (.D(loadB), .clk(clock_1_out), .enable(enable), .Q(fourbitreg_2_q));
  ALU alu_1 (
    .A(fourbitreg_1_q), .B(fourbitreg_2_q), .OP(priority_encoder_1_out), .C(out_10), .Z(out_11), .N(out_12),
    .V(out_13), .S(alu_1_s));
  fourBitRestricted fourbitrestricted_1 (
    .data(alu_1_s), .clk(clock_1_out), .load(priority_encoder_1_gs), .read(read), .Q(Q));  // open: nQ
endmodule

module fourBitReg (
  input  [3:0] D,
  input  clk,
  input  enable,
  output [3:0] Q
);

  FFD ffd_1 (.D(D[3]), .clk(clk), .enable(enable), .Q(Q[3]));  // open: nQ
  FFD ffd_2 (.D(D[2]), .clk(clk), .enable(enable), .Q(Q[2]));  // open: nQ
  FFD ffd_3 (.D(D[1]), .clk(clk), .enable(enable), .Q(Q[1]));  // open: nQ
  FFD ffd_4 (.D(D[0]), .clk(clk), .enable(enable), .Q(Q[0]));  // open: nQ
endmodule

module fourBitRegBetter (
  input  [3:0] D,
  input  clk,
  input  enable,
  output [3:0] Q,
  output [3:0] nQ
);

  wire and_1_out;

  and and_1 (and_1_out, clk, enable);
  D_Flip_Flop d_ff_1 (.D(D[3]), .clk(and_1_out), .Q(Q[3]), .Qn(nQ[3]));  // open: preset, reset
  D_Flip_Flop d_ff_2 (.D(D[2]), .clk(and_1_out), .Q(Q[2]), .Qn(nQ[2]));  // open: preset, reset
  D_Flip_Flop d_ff_3 (.D(D[1]), .clk(and_1_out), .Q(Q[1]), .Qn(nQ[1]));  // open: preset, reset
  D_Flip_Flop d_ff_4 (.D(D[0]), .clk(and_1_out), .Q(Q[0]), .Qn(nQ[0]));  // open: preset, reset
endmodule

module fourBitRestricted (
  input  [3:0] data,
  input  clk,
  input  load,
  input  read,
  output [3:0] Q,
  output [3:0] nQ
);

  wire [3:0] fourbitregbetter_1_nq, fourbitregbetter_1_q;

  fourBitRegBetter fourbitregbetter_1 (
    .D(data), .clk(clk), .enable(load), .Q(fourbitregbetter_1_q), .nQ(fourbitregbetter_1_nq));
  assign nQ = read ? fourbitregbetter_1_nq : 4'bz;  // Controlled_Buffer controlled_buffer_1
  assign Q = read ? fourbitregbetter_1_q : 4'bz;  // Controlled_Buffer controlled_buffer_2
endmodule

module fourBitBidirectional (
  input  clk,
  input  load,
  input  read,
  input  [3:0] D,
  output [3:0] out_5
);

  wire [3:0] controlled_buffer_1_out, fourbitrestricted_1_q;

  assign controlled_buffer_1_out = load ? D : 4'bz;  // Controlled_Buffer controlled_buffer_1
  fourBitRestricted fourbitrestricted_1 (
    .data(controlled_buffer_1_out), .clk(clk), .load(load), .read(read), .Q(fourbitrestricted_1_q));  // open: nQ
  assign out_5 = read ? fourbitrestricted_1_q : 4'bz;  // Controlled_Buffer controlled_buffer_2
endmodule

module collatz (
  input  [4:0] numberIn,
  output [4:0] numberOut
);

  wire not_1_out, priority_encoder_1_p2;
  wire [4:0] demultiplexer_1_out0, demultiplexer_1_out1, divider_1_out, multiplier_1_out;

  Demultiplexer #(.width(5)) demultiplexer_1 (
    .out0(demultiplexer_1_out0), .out1(demultiplexer_1_out1), .in(numberIn), .sel(priority_encoder_1_p2));
  not not_1 (not_1_out, numberIn[0]);
  // Priority_Encoder #(.select(1)) priority_encoder_1: pin names not known; wires that end beside it: not_1_out, priority_encoder_1_p2, numberIn[0]
  Multiplier #(.width(5)) multiplier_1 (
    .a(demultiplexer_1_out1), .b(5'b00011), .out(multiplier_1_out), .cin(5'b00001));  // open: cout
  Divider #(.width(5)) divider_1 (.a(demultiplexer_1_out0), .b(5'b00010), .out(divider_1_out));  // open: upper, rem
  assign numberOut = numberIn[0] ? multiplier_1_out : 5'bz;  // Controlled_Buffer controlled_buffer_1
  assign numberOut = not_1_out ? divider_1_out : 5'bz;  // Controlled_Buffer controlled_buffer_2
endmodule

module seqCollatz (
  input  in_1,
  input  [4:0] in_2
);

  wire clock_1_out, comparator_1_eq, not_1_out, not_8_out;
  wire [4:0] collatz_1_numberout, controlled_buffer_1_out, not_2_out, not_3_out, not_4_out, not_5_out,
       not_6_out, not_7_out, register_1_q, register_2_q;

  Clock clock_1 (.out(clock_1_out));
  assign controlled_buffer_1_out = in_1 ? in_2 : 5'bz;  // Controlled_Buffer controlled_buffer_1
  Register #(.width(5)) register_1 (.D(controlled_buffer_1_out), .clk(clock_1_out), .Q(register_1_q));  // open: en, clr
  not not_1 (not_1_out, in_1);
  assign controlled_buffer_1_out = not_1_out ? not_2_out : 5'bz;  // Controlled_Buffer controlled_buffer_2
  assign not_2_out = ~not_3_out;  // NOT_Gate not_2, 5 bits wide
  assign not_3_out = ~not_4_out;  // NOT_Gate not_3, 5 bits wide
  assign not_4_out = ~not_5_out;  // NOT_Gate not_4, 5 bits wide
  assign not_5_out = ~not_6_out;  // NOT_Gate not_5, 5 bits wide
  collatz collatz_1 (.numberIn(register_1_q), .numberOut(collatz_1_numberout));
  assign not_6_out = ~not_7_out;  // NOT_Gate not_6, 5 bits wide
  assign not_7_out = ~register_2_q;  // NOT_Gate not_7, 5 bits wide
  not not_8 (not_8_out, comparator_1_eq);
  Register #(.width(5)) register_2 (
    .D(collatz_1_numberout), .en(not_8_out), .clk(clock_1_out), .Q(register_2_q), .clr(in_1));
  Comparator #(.mode("unsigned"), .width(5)) comparator_1 (
    .a(register_2_q), .b(5'b00001), .eq(comparator_1_eq));  // open: gt, lt
endmodule
